// Logisim project cpu.circ as structural Verilog: 3 circuits, main circuit datapath
module datapath (
  input  pcsrc,
  input  mdrload,
  input  mem2reg,
  input  pcload,
  input  regwrite,
  input  [2:0] opc,
  input  sub,
  input  IOrD,
  input  ALoad,
  input  alusrc1,
  input  regsrc2,
  input  aluoutload,
  input  IRload,
  input  [4:0] rs1,
  input  [4:0] rs2,
  input  [4:0] rd,
  input  BLoad,
  input  [1:0] alusrc2,
  input  MemWr,
  input  MemRd,
  input  [31:0] imm,
  input  [1:0] width,
  input  Extend,
  input  in_24,
  output [31:0] ALU_Out,
  output z,
  output c,
  output [31:0] Inst
);

  wire cd, pull_resistor_1_node;
  wire [4:0] multiplexer_4_out;
  wire [31:0] alu_1_res, b, memory_1_data, multiplexer_1_out, multiplexer_2_out, multiplexer_3_out,
       multiplexer_5_out, multiplexer_6_out, regfile_1_r1_d, regfile_1_r2_d, register_1_q, register_2_q,
       register_4_q;

  Multiplexer #(.width(32), .enable("false")) multiplexer_1 (
    .in0(ALU_Out), .in1(alu_1_res), .out(multiplexer_1_out), .sel(pcsrc));
  Register #(.width(32)) register_1 (.D(multiplexer_1_out), .en(pcload), .Q(register_1_q), .clk(in_24));  // open: clr
  Multiplexer #(.width(32), .enable("false")) multiplexer_2 (
    .in0(register_1_q), .in1(b), .out(multiplexer_2_out), .sel(IOrD));
  Memory memory_1 (
    .Address(multiplexer_2_out), .Input(b), .Clock(in_24), .Clear(pull_resistor_1_node), .Load(MemRd),
    .Store(MemWr), .Data(memory_1_data), .Width(width), .Extend(Extend), .DClock(cd));
  Pull_Resistor pull_resistor_1 (.node(pull_resistor_1_node));
  Register #(.width(32)) register_2 (.D(memory_1_data), .en(mdrload), .Q(register_2_q), .clk(cd));  // open: clr
  Register #(.width(32)) register_3 (.D(memory_1_data), .en(IRload), .Q(Inst), .clk(cd));  // open: clr
  Multiplexer #(.width(32), .enable("false")) multiplexer_3 (
    .in0(ALU_Out), .in1(register_2_q), .out(multiplexer_3_out), .sel(mem2reg));
  Multiplexer #(.width(5), .enable("false")) multiplexer_4 (
    .in0(rs2), .in1(rd), .out(multiplexer_4_out), .sel(regsrc2));
  regfile regfile_1 (
    .wr(multiplexer_3_out), .r1_a(rs1), .r1_d(regfile_1_r1_d), .r2_a(multiplexer_4_out),
    .r2_d(regfile_1_r2_d), .w_a(rd), .e_en(regwrite), .clk(in_24));
  Register #(.width(32)) register_4 (.D(regfile_1_r1_d), .en(ALoad), .Q(register_4_q), .clk(in_24));  // open: clr
  Register #(.width(32)) register_5 (.D(regfile_1_r2_d), .en(BLoad), .Q(b), .clk(in_24));  // open: clr
  Multiplexer #(.width(32), .enable("false")) multiplexer_5 (
    .in0(register_1_q), .in1(register_4_q), .out(multiplexer_5_out), .sel(alusrc1));
  ALU alu_1 (.Op1(multiplexer_5_out), .op2(multiplexer_6_out), .Sub(sub), .Opcode(opc), .Res(alu_1_res), .C(c), .Z(z));
  Multiplexer #(.select(2), .width(32), .enable("false")) multiplexer_6 (
    .in0(32'h4), .in1(b), .in2(imm), .out(multiplexer_6_out), .sel(alusrc2));  // open: in3
  Register #(.width(32)) register_6 (.D(alu_1_res), .en(aluoutload), .Q(ALU_Out), .clk(in_24));  // open: clr

  // Other names for the same wires on the sheet: clk = in_24
endmodule

module control_unit (
  input  [31:0] alu_out,
  input  clk,
  input  [31:0] inst_in,
  input  z_in,
  input  c_in,
  output ALU_Src1,
  output [1:0] ALU_Src2,
  output PC_Src,
  output [2:0] ALU_Op,
  output Sub,
  output I_Or_D,
  output Mem_Read,
  output IR_Load,
  output [31:0] imm,
  output ALU_Out_Ld,
  output halt,
  output A_Load,
  output B_Load,
  output [4:0] rs1,
  output [4:0] rs2,
  output [4:0] rd,
  output Mem2Reg,
  output Reg_Write,
  output Reg_Src_2,
  output PC_Load,
  output mdr_load,
  output [1:0] width,
  output extend,
  output memwr
);

  wire and_20_out, and_21_out, and_22_out, and_23_out, and_24_out, and_25_out, and_26_out, and_27_out,
       and_28_out, and_29_out, and_30_out, and_31_out, and_32_out, and_33_out, and_34_out, and_35_out,
       and_36_out, and_37_out, and_38_out, and_39_out, and_40_out, and_41_out, and_42_out, and_43_out,
       and_44_out, and_45_out, and_46_out, AUIPC, BRANCH, branch_z, D_Phase, decoder_1_out0, decoder_1_out1,
       decoder_1_out3, decoder_2_out0, decoder_2_out1, decoder_2_out3, decoder_2_out4, decoder_2_out5,
       decoder_3_out0, decoder_3_out1, decoder_3_out4, decoder_3_out5, decoder_3_out6, decoder_3_out7,
       decoder_4_out0, decoder_4_out4, decoder_4_out6, decoder_5_out0, decoder_5_out2, decoder_5_out3,
       decoder_5_out4, JAL, JALR, LOAD, LUI, MISC_MEM, nor_1_out, OP, OP_IMM, or_1_out, or_2_out, or_3_out,
       or_5_out, or_6_out, or_7_out, or_10_out, or_11_out, or_12_out, or_13_out, or_14_out, or_15_out,
       or_16_out, or_17_out, or_18_out, STORE, SYSTEM, tty_write, valid_opc, xnor_1_out;
  wire [2:0] and_17_out, and_18_out, and_19_out, bit_extender_6_out, bit_extender_7_out, bit_extender_8_out,
       branch_type, counter_1_q;
  wire [6:0] tty_data;
  wire [19:0] and_14_out, and_15_out, and_16_out, bit_extender_3_out, bit_extender_4_out, bit_extender_5_out,
       imm_i, imm_s_sb, or_4_out;
  wire [31:0] imm_t;

  Pull_Resistor pull_resistor_1 (.node(alu_out));
  Pull_Resistor pull_resistor_2 (.node(inst_in));
  Decoder #(.select(2), .disabled(0)) decoder_1 (
    .out0(decoder_1_out0), .out1(decoder_1_out1), .out3(decoder_1_out3), .sel(inst_in[6:5]), .en(valid_opc));  // open: out2
  Pull_Resistor pull_resistor_3 (.node(z_in));
  Pull_Resistor pull_resistor_4 (.node(c_in));
  and and_1 (valid_opc, inst_in[0], inst_in[1]);
  Decoder #(.select(3), .disabled(0)) decoder_2 (
    .out0(decoder_2_out0), .out1(decoder_2_out1), .out3(decoder_2_out3), .out4(decoder_2_out4),
    .out5(decoder_2_out5), .sel(inst_in[4:2]), .en(valid_opc));  // open: out2, out6, out7
  and and_2 (LOAD, decoder_1_out0, decoder_2_out0);
  and and_3 (STORE, decoder_1_out1, decoder_2_out0);
  and and_4 (BRANCH, decoder_1_out3, decoder_2_out0);
  Pull_Resistor pull_resistor_5 (.node(tty_data));
  TTY tty_1 (.data(tty_data), .clk(clk), .we(tty_write));  // open: clr
  Pull_Resistor pull_resistor_6 (.node(tty_write));
  and and_5 (OP_IMM, decoder_1_out0, decoder_2_out4);
  and and_6 (MISC_MEM, decoder_1_out0, decoder_2_out3);
  and and_7 (OP, decoder_1_out1, decoder_2_out4);
  and and_8 (LUI, decoder_1_out1, decoder_2_out5);
  and and_9 (JALR, decoder_2_out1, decoder_1_out3);
  and and_10 (JAL, decoder_2_out3, decoder_1_out3);
  and and_11 (AUIPC, decoder_1_out0, decoder_2_out5);
  and and_12 (SYSTEM, decoder_2_out4, decoder_1_out3);
  nor nor_1 (nor_1_out, MISC_MEM, LOAD, OP_IMM, AUIPC, STORE, OP, LUI, BRANCH, JALR, JAL, SYSTEM);
  and and_13 (halt, D_Phase, nor_1_out);
  or or_1 (or_1_out, AUIPC, LUI, JAL);
  or or_2 (or_2_out, STORE, BRANCH);
  or or_3 (or_3_out, LOAD, JALR, OP_IMM);
  assign imm_s_sb = {{13{inst_in[31]}}, inst_in[31:25]};  // Bit_Extender bit_extender_1
  assign imm_i = {{8{inst_in[31]}}, inst_in[31:20]};  // Bit_Extender bit_extender_2
  assign bit_extender_3_out = {{19{or_1_out}}, or_1_out};  // Bit_Extender bit_extender_3
  assign bit_extender_4_out = {{19{or_2_out}}, or_2_out};  // Bit_Extender bit_extender_4
  assign bit_extender_5_out = {{19{or_3_out}}, or_3_out};  // Bit_Extender bit_extender_5
  assign and_14_out = inst_in[31:12] & bit_extender_3_out;  // AND_Gate and_14, 20 bits wide
  assign and_15_out = imm_s_sb & bit_extender_4_out;  // AND_Gate and_15, 20 bits wide
  assign and_16_out = imm_i & bit_extender_5_out;  // AND_Gate and_16, 20 bits wide
  Decoder #(.select(3), .enable("false")) decoder_3 (
    .out0(decoder_3_out0), .out1(decoder_3_out1), .out4(decoder_3_out4), .out5(decoder_3_out5),
    .out6(decoder_3_out6), .out7(decoder_3_out7), .sel(inst_in[14:12]));  // open: out2, out3
  Decoder #(.select(3), .enable("false")) decoder_4 (
    .out0(decoder_4_out0), .out4(decoder_4_out4), .out6(decoder_4_out6), .sel(inst_in[14:12]));  // open: out1, out2, out3, out5, out7
  assign or_4_out = and_14_out | and_15_out | and_16_out;  // OR_Gate or_4, 20 bits wide
  or or_5 (or_5_out, decoder_3_out0, decoder_3_out1);
  assign bit_extender_6_out = {{2{or_5_out}}, or_5_out};  // Bit_Extender bit_extender_6
  assign bit_extender_7_out = {{2{or_6_out}}, or_6_out};  // Bit_Extender bit_extender_7
  or or_6 (or_6_out, decoder_3_out4, decoder_3_out5);
  assign bit_extender_8_out = {{2{or_7_out}}, or_7_out};  // Bit_Extender bit_extender_8
  or or_7 (or_7_out, decoder_3_out6, decoder_3_out7);
  or or_8 (branch_z, decoder_4_out0, decoder_4_out4, decoder_4_out6);
  Pull_Resistor pull_resistor_7 (.node(ALU_Src1));
  Pull_Resistor pull_resistor_8 (.node(ALU_Src2));
  Pull_Resistor pull_resistor_9 (.node(PC_Src));
  Pull_Resistor pull_resistor_10 (.node(ALU_Op));
  Pull_Resistor pull_resistor_11 (.node(Sub));
  Pull_Resistor pull_resistor_12 (.node(I_Or_D));
  Pull_Resistor pull_resistor_13 (.node(Mem_Read));
  Pull_Resistor pull_resistor_14 (.node(IR_Load));
  Pull_Resistor pull_resistor_15 (.node(imm));
  Pull_Resistor pull_resistor_16 (.node(ALU_Out_Ld));
  Pull_Resistor pull_resistor_17 (.node(A_Load));
  Pull_Resistor pull_resistor_18 (.node(B_Load));
  Pull_Resistor pull_resistor_19 (.node(rs1));
  Pull_Resistor pull_resistor_20 (.node(rs2));
  Pull_Resistor pull_resistor_21 (.node(rd));
  Pull_Resistor pull_resistor_22 (.node(Mem2Reg));
  Pull_Resistor pull_resistor_23 (.node(Reg_Write));
  Pull_Resistor pull_resistor_24 (.node(Reg_Src_2));
  Pull_Resistor pull_resistor_25 (.node(PC_Load));
  Pull_Resistor pull_resistor_26 (.node(mdr_load));
  Pull_Resistor pull_resistor_27 (.node(width));
  Pull_Resistor pull_resistor_28 (.node(extend));
  Pull_Resistor pull_resistor_29 (.node(memwr));
  assign imm_t = {{12{or_4_out[19]}}, or_4_out};  // Bit_Extender bit_extender_9
  assign and_17_out = bit_extender_6_out & 3'b100;  // AND_Gate and_17, 3 bits wide
  assign and_18_out = bit_extender_7_out & 3'b010;  // AND_Gate and_18, 3 bits wide
  assign and_19_out = bit_extender_8_out & 3'b011;  // AND_Gate and_19, 3 bits wide
  assign branch_type = and_17_out | and_18_out | and_19_out;  // OR_Gate or_9, 3 bits wide
  buf buffer_1 (PC_Load, decoder_5_out0);
  buf buffer_2 (PC_Src, decoder_5_out0);
  buf buffer_3 (Mem_Read, decoder_5_out0);
  buf buffer_4 (IR_Load, decoder_5_out0);
  or or_10 (or_10_out, JALR, JAL);
  and and_20 (and_20_out, D_Phase, or_10_out);
  or or_11 (or_11_out, JALR, OP_IMM);
  and and_21 (and_21_out, D_Phase, or_11_out);
  or or_12 (or_12_out, LUI, AUIPC);
  and and_22 (and_22_out, D_Phase, or_12_out);
  and and_23 (and_23_out, D_Phase, BRANCH);
  buf buffer_5 (ALU_Out_Ld, and_23_out);
  buf buffer_6 (A_Load, and_23_out);
  buf buffer_7 (B_Load, and_23_out);
  and and_24 (and_24_out, D_Phase, OP);
  and and_25 (and_25_out, D_Phase, SYSTEM);
  buf buffer_8 (B_Load, and_25_out);
  buf buffer_9 (A_Load, and_25_out);
  or or_13 (or_13_out, STORE, LOAD);
  and and_26 (and_26_out, D_Phase, or_13_out);
  and and_27 (and_27_out, D_Phase, STORE);
  Multiplexer #(.width(2), .enable("false")) multiplexer_1 (
    .in1(2'b10), .out(ALU_Src2), .sel(and_20_out));  // open: in0
  buf buffer_10 (ALU_Out_Ld, and_20_out);
  buf buffer_11 (A_Load, and_21_out);
  Multiplexer #(.width(5), .enable("false")) multiplexer_2 (
    .in1(inst_in[19:15]), .out(rs1), .sel(and_21_out));  // open: in0
  buf buffer_12 (A_Load, and_22_out);
  Multiplexer #(.width(2), .enable("false")) multiplexer_3 (
    .in1(2'b10), .out(ALU_Src2), .sel(and_23_out));  // open: in0
  buf buffer_13 (A_Load, and_24_out);
  buf buffer_14 (B_Load, and_24_out);
  Multiplexer #(.width(5), .enable("false")) multiplexer_4 (.in1(5'b01010), .out(rs1), .sel(and_25_out));  // open: in0
  buf buffer_15 (A_Load, and_26_out);
  Multiplexer #(.width(5), .enable("false")) multiplexer_5 (
    .in1(inst_in[19:15]), .out(rs1), .sel(and_26_out));  // open: in0
  buf buffer_16 (B_Load, and_27_out);
  Multiplexer #(.width(5), .enable("false")) multiplexer_6 (
    .in1(inst_in[24:20]), .out(rs2), .sel(and_27_out));  // open: in0
  Decoder #(.select(3), .enable("false")) decoder_5 (
    .out0(decoder_5_out0), .out1(D_Phase), .out2(decoder_5_out2), .out3(decoder_5_out3),
    .out4(decoder_5_out4), .sel(counter_1_q));  // open: out5, out6, out7
  Counter #(.width(3), .max('h4), .trigger("falling")) counter_1 (
    .Q(counter_1_q), .clk(clk));  // open: load, D, count, carry, clr
  or or_14 (or_14_out, JALR, JAL);
  and and_28 (and_28_out, decoder_5_out2, or_14_out);
  buf buffer_17 (Reg_Write, and_28_out);
  and and_29 (and_29_out, decoder_5_out2, BRANCH);
  buf buffer_18 (Sub, and_29_out);
  and and_30 (and_30_out, decoder_5_out2, LUI);
  buf buffer_19 (ALU_Src1, and_30_out);
  buf buffer_20 (ALU_Out_Ld, and_30_out);
  and and_31 (and_31_out, decoder_5_out2, AUIPC);
  buf buffer_21 (ALU_Out_Ld, and_31_out);
  and and_32 (and_32_out, decoder_5_out2, OP);
  Multiplexer #(.width(3), .enable("false")) multiplexer_7 (
    .in1(inst_in[14:12]), .out(ALU_Op), .sel(and_32_out));  // open: in0
  Multiplexer #(.enable("false")) multiplexer_8 (.in1(inst_in[30]), .out(Sub), .sel(and_32_out));  // open: in0
  or or_15 (or_15_out, STORE, LOAD);
  and and_33 (and_33_out, decoder_5_out2, or_15_out);
  buf buffer_22 (ALU_Src1, and_33_out);
  buf buffer_23 (ALU_Out_Ld, and_33_out);
  Multiplexer #(.width(5), .enable("false")) multiplexer_9 (
    .in1(inst_in[11:7]), .out(rd), .sel(and_28_out));  // open: in0
  Multiplexer #(.width(3), .enable("false")) multiplexer_10 (
    .in1(branch_type), .out(ALU_Op), .sel(and_29_out));  // open: in0
  Multiplexer #(.width(2), .enable("false")) multiplexer_11 (
    .in1(2'b10), .out(ALU_Src2), .sel(and_30_out));  // open: in0
  Multiplexer #(.width(2), .enable("false")) multiplexer_12 (
    .in1(2'b10), .out(ALU_Src2), .sel(and_31_out));  // open: in0
  Multiplexer #(.width(32), .enable("false")) multiplexer_13 (.in1(imm_t), .out(imm), .sel(and_31_out));  // open: in0
  Multiplexer #(.width(2), .enable("false")) multiplexer_14 (
    .in1(2'b10), .out(ALU_Src2), .sel(and_33_out));  // open: in0
  Multiplexer #(.width(32), .enable("false")) multiplexer_15 (.in1(imm_t), .out(imm), .sel(and_33_out));  // open: in0
  and and_34 (and_34_out, decoder_5_out3, JAL);
  buf buffer_24 (ALU_Out_Ld, and_34_out);
  Multiplexer #(.width(2), .enable("false")) multiplexer_16 (
    .in1(2'b10), .out(ALU_Src2), .sel(and_34_out));  // open: in0
  and and_35 (and_35_out, decoder_5_out3, JALR);
  buf buffer_25 (ALU_Out_Ld, and_35_out);
  buf buffer_26 (ALU_Src1, and_35_out);
  Multiplexer #(.width(2), .enable("false")) multiplexer_17 (
    .in1(2'b10), .out(ALU_Src2), .sel(and_35_out));  // open: in0
  and and_36 (and_36_out, decoder_5_out3, OP);
  buf buffer_27 (ALU_Out_Ld, and_36_out);
  and and_37 (and_37_out, decoder_5_out3, SYSTEM);
  buf buffer_28 (ALU_Src1, and_37_out);
  buf buffer_29 (ALU_Out_Ld, and_37_out);
  Multiplexer #(.width(2), .enable("false")) multiplexer_18 (
    .in1(2'b01), .out(ALU_Src2), .sel(and_37_out));  // open: in0
  and and_38 (and_38_out, decoder_5_out3, OP_IMM);
  Multiplexer #(.width(2), .enable("false")) multiplexer_19 (
    .in1(2'b10), .out(ALU_Src2), .sel(and_38_out));  // open: in0
  buf buffer_30 (ALU_Src1, and_38_out);
  Multiplexer #(.width(3), .enable("false")) multiplexer_20 (
    .in1(inst_in[14:12]), .out(ALU_Op), .sel(and_38_out));  // open: in0
  Multiplexer #(.enable("false")) multiplexer_21 (.in1(inst_in[30]), .out(Sub), .sel(and_38_out));  // open: in0
  Multiplexer #(.width(32), .enable("false")) multiplexer_22 (.in1(imm_t), .out(imm), .sel(and_38_out));  // open: in0
  buf buffer_31 (ALU_Out_Ld, and_38_out);
  and and_39 (and_39_out, decoder_5_out3, STORE);
  buf buffer_32 (memwr, and_39_out);
  buf buffer_33 (I_Or_D, and_39_out);
  Multiplexer #(.width(2), .enable("false")) multiplexer_23 (
    .in1(inst_in[13:12]), .out(width), .sel(and_39_out));  // open: in0
  and and_40 (and_40_out, decoder_5_out3, LOAD);
  buf buffer_34 (mdr_load, and_40_out);
  buf buffer_35 (Mem_Read, and_40_out);
  buf buffer_36 (I_Or_D, and_40_out);
  Multiplexer #(.width(2), .enable("false")) multiplexer_24 (
    .in1(inst_in[13:12]), .out(width), .sel(and_40_out));  // open: in0
  Multiplexer #(.enable("false")) multiplexer_25 (.in1(inst_in[14]), .out(extend), .sel(and_40_out));  // open: in0
  or or_16 (or_16_out, JAL, JALR);
  and and_41 (and_41_out, decoder_5_out4, or_16_out);
  buf buffer_37 (PC_Load, and_41_out);
  xnor xnor_1 (xnor_1_out, z_in, branch_z);
  and and_42 (and_42_out, decoder_5_out4, BRANCH, xnor_1_out);
  buf buffer_38 (PC_Load, and_42_out);
  or or_17 (or_17_out, LUI, AUIPC);
  and and_43 (and_43_out, decoder_5_out4, or_17_out);
  buf buffer_39 (PC_Load, and_43_out);
  or or_18 (or_18_out, OP_IMM, OP);
  and and_44 (and_44_out, decoder_5_out4, or_18_out);
  buf buffer_40 (Reg_Write, and_44_out);
  Multiplexer #(.width(5), .enable("false")) multiplexer_26 (
    .in1(inst_in[11:7]), .out(rd), .sel(and_44_out));  // open: in0
  and and_45 (and_45_out, decoder_5_out4, SYSTEM);
  buf buffer_41 (tty_write, and_45_out);
  and and_46 (and_46_out, decoder_5_out4, LOAD);
  buf buffer_42 (Reg_Write, and_46_out);
  Multiplexer #(.width(5), .enable("false")) multiplexer_27 (
    .in1(inst_in[11:7]), .out(rd), .sel(and_46_out));  // open: in0
  buf buffer_43 (Mem2Reg, and_46_out);
  Multiplexer #(.width(7), .enable("false")) multiplexer_28 (
    .in1(alu_out[6:0]), .out(tty_data), .sel(and_45_out));  // open: in0

  // Other names for the same wires on the sheet: ALU_Op_out[2:0] = ALU_Op; c = c_in; imm_out[31:0] = imm;
  //   inst[31:0] = inst_in; inst_4_2[2:0] = inst_in[4:2]; inst_6_5[1:0] = inst_in[6:5]; rd_t[4:0] = inst_in[11:7];
  //   funct3[2:0] = inst_in[14:12]; imm_u_uj[19:0] = inst_in[31:12]; rs1_t[4:0] = inst_in[19:15];
  //   rs2_t[4:0] = inst_in[24:20]; funct7[6:0] = inst_in[31:25]; Mdr_Ld = mdr_load; rd_out[4:0] = rd;
  //   rs1_out[4:0] = rs1; rs2_out[4:0] = rs2; sub_out = Sub; z = z_in

  // Notes on the sheet:
  //   Decode Opc:
  //   inputs:
  //   determine halt:
  //   Split Inst:
  //   determine immediate:
  //   determine branch type:
  //   Outputs:
  //   pc=pc+4
  //   IR <- Mem[PC]
  //   Fetch
  //   buffer_1 drives only 1 and floats otherwise
  //   buffer_2 drives only 1 and floats otherwise
  //   buffer_3 drives only 1 and floats otherwise
  //   buffer_4 drives only 1 and floats otherwise
  //   UJ/JALR:
  //   (PC)
  //   I-Type:
  //   U-Type:
  //   SB-Type:
  //   R-Type:
  //   System:
  //   Load/Store:
  //   D
  //   buffer_5 drives only 1 and floats otherwise
  //   buffer_6 drives only 1 and floats otherwise
  //   buffer_7 drives only 1 and floats otherwise
  //   buffer_8 drives only 1 and floats otherwise
  //   buffer_9 drives only 1 and floats otherwise
  //   buffer_10 drives only 1 and floats otherwise
  //   buffer_11 drives only 1 and floats otherwise
  //   buffer_12 drives only 1 and floats otherwise
  //   buffer_13 drives only 1 and floats otherwise
  //   buffer_14 drives only 1 and floats otherwise
  //   buffer_15 drives only 1 and floats otherwise
  //   buffer_16 drives only 1 and floats otherwise
  //   UJ/JALR:
  //   SB-Type:
  //   LUI:
  //   AUIPC:
  //   R-Type:
  //   Load/Store:
  //   Instructions:
  //   X
  //   buffer_17 drives only 1 and floats otherwise
  //   buffer_18 drives only 1 and floats otherwise
  //   buffer_19 drives only 1 and floats otherwise
  //   buffer_20 drives only 1 and floats otherwise
  //   buffer_21 drives only 1 and floats otherwise
  //   buffer_22 drives only 1 and floats otherwise
  //   buffer_23 drives only 1 and floats otherwise
  //   M
  //   UJ:
  //   JALR:
  //   R/I-Type:
  //   System:
  //   I-Type:
  //   buffer_24 drives only 1 and floats otherwise
  //   buffer_25 drives only 1 and floats otherwise
  //   buffer_26 drives only 1 and floats otherwise
  //   buffer_27 drives only 1 and floats otherwise
  //   buffer_28 drives only 1 and floats otherwise
  //   buffer_29 drives only 1 and floats otherwise
  //   buffer_30 drives only 1 and floats otherwise
  //   buffer_31 drives only 1 and floats otherwise
  //   buffer_32 drives only 1 and floats otherwise
  //   buffer_33 drives only 1 and floats otherwise
  //   buffer_34 drives only 1 and floats otherwise
  //   buffer_35 drives only 1 and floats otherwise
  //   buffer_36 drives only 1 and floats otherwise
  //   W
  //   UJ/JALR:
  //   SB-Type:
  //   U-Type:
  //   R/I-Type:
  //   System:
  //   buffer_37 drives only 1 and floats otherwise
  //   buffer_38 drives only 1 and floats otherwise
  //   buffer_39 drives only 1 and floats otherwise
  //   buffer_40 drives only 1 and floats otherwise
  //   buffer_41 drives only 1 and floats otherwise
  //   buffer_42 drives only 1 and floats otherwise
  //   buffer_43 drives only 1 and floats otherwise
endmodule

module main (
  output halt
);

  wire clock_1_out, control_unit_1_a_load, control_unit_1_alu_out_ld, control_unit_1_alu_src1,
       control_unit_1_b_load, control_unit_1_extend, control_unit_1_i_or_d, control_unit_1_ir_load,
       control_unit_1_mdr_load, control_unit_1_mem2reg, control_unit_1_mem_read, control_unit_1_memwr,
       control_unit_1_pc_load, control_unit_1_pc_src, control_unit_1_reg_src_2, control_unit_1_reg_write,
       control_unit_1_sub, datapath_1_c, datapath_1_z;
  wire [1:0] control_unit_1_alu_src2, control_unit_1_width;
  wire [2:0] control_unit_1_alu_op;
  wire [4:0] control_unit_1_rd, control_unit_1_rs1, control_unit_1_rs2;
  wire [31:0] control_unit_1_imm, datapath_1_alu_out, datapath_1_inst;

  Clock clock_1 (.out(clock_1_out));
  control_unit control_unit_1 (
    .z_in(datapath_1_z), .ALU_Src1(control_unit_1_alu_src1), .c_in(datapath_1_c),
    .ALU_Src2(control_unit_1_alu_src2), .PC_Src(control_unit_1_pc_src), .ALU_Op(control_unit_1_alu_op),
    .clk(clock_1_out), .Sub(control_unit_1_sub), .inst_in(datapath_1_inst), .I_Or_D(control_unit_1_i_or_d),
    .Mem_Read(control_unit_1_mem_read), .IR_Load(control_unit_1_ir_load), .imm(control_unit_1_imm),
    .ALU_Out_Ld(control_unit_1_alu_out_ld), .A_Load(control_unit_1_a_load), .B_Load(control_unit_1_b_load),
    .rs1(control_unit_1_rs1), .rs2(control_unit_1_rs2), .rd(control_unit_1_rd),
    .Mem2Reg(control_unit_1_mem2reg), .Reg_Write(control_unit_1_reg_write),
    .Reg_Src_2(control_unit_1_reg_src_2), .PC_Load(control_unit_1_pc_load),
    .mdr_load(control_unit_1_mdr_load), .halt(halt), .alu_out(datapath_1_alu_out),
    .width(control_unit_1_width), .extend(control_unit_1_extend), .memwr(control_unit_1_memwr));
  datapath datapath_1 (
    .pcload(control_unit_1_pc_load), .in_24(clock_1_out), .alusrc1(control_unit_1_alu_src1),
    .alusrc2(control_unit_1_alu_src2), .mdrload(control_unit_1_mdr_load), .mem2reg(control_unit_1_mem2reg),
    .regwrite(control_unit_1_reg_write), .ALoad(control_unit_1_a_load), .opc(control_unit_1_alu_op),
    .sub(control_unit_1_sub), .pcsrc(control_unit_1_pc_src), .MemWr(control_unit_1_memwr),
    .IOrD(control_unit_1_i_or_d), .IRload(control_unit_1_ir_load), .Inst(datapath_1_inst),
    .regsrc2(control_unit_1_reg_src_2), .rs1(control_unit_1_rs1), .rs2(control_unit_1_rs2),
    .rd(control_unit_1_rd), .BLoad(control_unit_1_b_load), .imm(control_unit_1_imm), .z(datapath_1_z),
    .c(datapath_1_c), .MemRd(control_unit_1_mem_read), .width(control_unit_1_width),
    .Extend(control_unit_1_extend), .aluoutload(control_unit_1_alu_out_ld), .ALU_Out(datapath_1_alu_out));
endmodule
